# Fritzing sketch Arduino Garage Ping (saved by Fritzing 0.9.2b)
breadboards: 2

parts:
  Part1 = Arduino Nano (Rev3.0)
  J2 = male pin header, 2 pins [form="♂ (male)"]
  J3 = male pin header, 2 pins [form="♂ (male)"]
  J1 = male pin header, 3 pins [form="♂ (male)"]
  J4 = Screw terminal - 2 pins [package=THT]
  J5 = Screw terminal - 2 pins [package=THT]
  J6 = Screw terminal - 2 pins [package=THT]
  Part3 = Dave HC-SR04
  Part4 = Dave HC-SR04
  J7 = Screw terminal - 2 pins [package=THT]
  J8 = double row male pin header, 2 pins [form="♂ (male)"]
  J9 = double row male pin header, 2 pins [form="♂ (male)"]

nets:
  N1: Part1.GND, J4.pin1, J5.pin2, J6.pin1
  N2: Part1.D2, J3.pin2
  N3: Part1.D3, J3.pin1
  N4: Part1.D7, J2.pin2
  N5: Part1.D8, J2.pin1
  N6: Part1.D10, J1.pin3
  N7: Part1.D11/MOSI, J1.pin2
  N8: Part1.D12/MISO, J1.pin1
  N9: Part1.VIN, J4.pin2, J5.pin1, J6.pin2
  VCC: Part3.VCC, Part4.VCC, J7.pin1
  N10: Part3.Trig, J8.pin1
  N11: Part3.Echo, J8.pin2
  GND: Part3.GND, Part4.GND, J7.pin2
  N12: Part4.Trig, J9.pin1
  N13: Part4.Echo, J9.pin2

notes:
  To R, Y, G Light Relays
  Sensor 2
  Sensor 1
  Power in
  Relay power
  Sensor power
  Garage Parking Assistant
